# Fritzing sketch HT_Meter (saved by Fritzing 0.9.2b)
breadboards: 1

parts:
  LCD1 = LCD screen
  RHT1 = Humidity and Temperature Sensor RHT03
  Part1 = Arduino Uno (Rev3)
  R1 = Resistor [tolerance=±5% resistance=10k package=THT]
  R2 = Resistor [tolerance=±5% resistance=330 package=THT]

nets:
  VSS: LCD1.VSS, LCD1.V0, LCD1.R/W, LCD1.LED-, RHT1.GND_2, Part1.GND
  VDD: LCD1.VDD, RHT1.Vcc, Part1.5V, R1.Pin_0, R2.Pin_0
  N1: LCD1.RS, Part1.D3_PWM
  N2: LCD1.E, Part1.D4
  N3: LCD1.DB4, Part1.D5_PWM
  N4: LCD1.DB5, Part1.D6_PWM
  N5: LCD1.DB6, Part1.D7
  N6: LCD1.DB7, Part1.D8
  N7: LCD1.LED+, R2.Pin_1
  N8: RHT1.Data-signal, Part1.D9_PWM, R1.Pin_1
